# Fritzing sketch 2 dot matrix  (saved by Fritzing 0.9.4)

parts:
  8x8_LED_Modul_mit_MAX1 = 8x8 LED Modul mit MAX7219 [package=THT]
  Part1 = Arduino Uno (Rev3)
  8x8_LED_Modul_mit_MAX2 = 8x8 LED Modul mit MAX7219 [package=THT]

nets:
  N1: 8x8_LED_Modul_mit_MAX1.VCC_Eingang, Part1.5V
  N2: 8x8_LED_Modul_mit_MAX1.GND_Eingang, Part1.GND
  N3: 8x8_LED_Modul_mit_MAX1.DIN_Eingang, Part1.D7
  N4: 8x8_LED_Modul_mit_MAX1.CS_Eingang, Part1.D5_PWM
  N5: 8x8_LED_Modul_mit_MAX1.CLK_Eingang, Part1.D6_PWM
  N6: 8x8_LED_Modul_mit_MAX1.VCC_Ausgang, 8x8_LED_Modul_mit_MAX2.VCC_Eingang
  N7: 8x8_LED_Modul_mit_MAX1.GND_Ausgang, 8x8_LED_Modul_mit_MAX2.GND_Eingang
  N8: 8x8_LED_Modul_mit_MAX1.DOUT_Ausgang, 8x8_LED_Modul_mit_MAX2.DIN_Eingang
  N9: 8x8_LED_Modul_mit_MAX1.CS_Ausgang, 8x8_LED_Modul_mit_MAX2.CS_Eingang
  N10: 8x8_LED_Modul_mit_MAX1.CLK_Ausgang, 8x8_LED_Modul_mit_MAX2.CLK_Eingang
